# Fritzing sketch circuit (saved by Fritzing 0.9.3b)
circuit board: 8.46667cm x 5.64444cm

parts:
  MOTOR1 = 28BYJ-48 Stepper Motor
  Part1 = Arduino Uno (Rev3) - ICSP
  MOTOR2 = 28BYJ-48 Stepper Motor
  BREAKOUT1 = ULN2003A breakout board
  BREAKOUT2 = ULN2003A breakout board

nets:
  N1: MOTOR1.RED, BREAKOUT1.RED_wire
  N2: MOTOR1.ORANGE, BREAKOUT1.ORANGE_wire
  N3: MOTOR1.YELLOW, BREAKOUT1.YELLOW_wire
  N4: MOTOR1.PINK, BREAKOUT1.PINK_wire
  N5: MOTOR1.BLUE, BREAKOUT1.BLUE_wire
  N6: Part1.D8, BREAKOUT1.In_4
  N7: Part1.D9_PWM, BREAKOUT1.In_3
  N8: Part1.D10_PWM/SS, BREAKOUT1.In_2
  N9: Part1.D11_PWM/MOSI, BREAKOUT1.In_1
  N10: Part1.D1/TX, BREAKOUT2.In_1
  N11: Part1.D2, BREAKOUT2.In_2
  N12: Part1.D3_PWM, BREAKOUT2.In_3
  N13: Part1.D4, BREAKOUT2.In_4
  N14: MOTOR2.RED, BREAKOUT2.RED_wire
  N15: MOTOR2.ORANGE, BREAKOUT2.ORANGE_wire
  N16: MOTOR2.YELLOW, BREAKOUT2.YELLOW_wire
  N17: MOTOR2.PINK, BREAKOUT2.PINK_wire
  N18: MOTOR2.BLUE, BREAKOUT2.BLUE_wire

custom parts:
  ULN2003A breakout board: ULN2003A 7-way Darlington Transistor Driver on breakoutboard
